# Fritzing sketch Diagrama_Electrico (saved by Fritzing 0.9.3b)
breadboards: 1

parts:
  Componente1 = Arduino Uno (Rev3)
  VCC2 = Battery block 9V
  U3 = HC-SR04 [chip_label=IC package="SIP (Single Inline) [THT]"]
  HC-6 = Bluetooth HC-05 Macho
  IC1 = L293D [package=THT]
  M1 = DC Motor
  M2 = DC Motor
  VCC3 = Battery
  J1 = Power Jack [package=power_jack_pth_lock]

nets:
  N1: Componente1.D8, IC1.In_3
  N2: Componente1.D9_PWM, IC1.Enable_2
  N3: Componente1.D10_PWM/SS, U3.Trig
  N4: Componente1.D11_PWM/MOSI, U3.Echo
  N5: Componente1.D2, HC-6.RXD
  N6: Componente1.D3_PWM, HC-6.TXD
  N7: Componente1.D4, IC1.In_1
  N8: Componente1.D5_PWM, IC1.Enable_1
  N9: Componente1.D6_PWM, IC1.In_2
  N10: Componente1.D7, IC1.In_4
  VCC: Componente1.5V, U3.Vcc, HC-6.VCC
  GND: Componente1.GND, U3.GND, HC-6.GND, IC1.0V, VCC3.-
  N11: VCC2.-, J1.GND
  N12: VCC2.+, J1.GNDBREAK
  N13: IC1.Out_1_(_Controlled_by_Enable_1_), M2.pin_2
  N14: IC1.Out_2_(_Controlled_by_Enable_1_), M2.pin_1
  N15: IC1.+Vmotor, IC1.+V, VCC3.+
  N16: IC1.Out_3_(_Controlled_by_Enable_2_), M1.pin_2
  N17: IC1.Out_4_(_Controlled_by_Enable_2_), M1.pin_1

custom parts:
  HC-SR04: HC-SR04 ultrasound distance sensor
